# Fritzing sketch simon_solder (saved by Fritzing 0.7.12b)
perfboards: 1

parts:
  J2 = Piezo Speaker
  U6 = Voltage Regulator - 5V [package="TO220 [THT]"]
  VCC1 = Battery block 9V
  C1 = Electrolytic Capacitor [capacitance=10µF package="100 mil [THT, electrolytic]"]
  C2 = Electrolytic Capacitor [capacitance=10µF package="100 mil [THT, electrolytic]"]
  U7 = atmega328 [package=dip]
  XTAL2 = Crystal [frequency="16 Mhz" package=THT]
  C5 = Ceramic Capacitor [capacitance=10pF package="0805 [SMD, multilayer]"]
  C6 = Ceramic Capacitor [capacitance=10pF package="0805 [SMD, multilayer]"]
  Button1 = Pushbutton [package="[THT]"]
  Button2 = Pushbutton [package="[THT]"]
  Button3 = Pushbutton [package="[THT]"]
  Button4 = Pushbutton [package="[THT]"]
  LED1 = LED - 5mm [color="Blue (430nm)" package="5 mm [THT]"]
  LED2 = LED - 5mm [color="White (6500K)" package="5 mm [THT]"]
  LED3 = LED - 5mm [color="Red (633nm)" package="5 mm [THT]"]
  LED4 = LED - 5mm [color="Green (555nm)" package="5 mm [THT]"]
  R1 = Resistor [tolerance=±5% resistance=220 package=THT]
  R2 = Resistor [tolerance=±5% resistance=220 package=THT]
  R3 = Resistor [tolerance=±5% resistance=220 package=THT]
  R4 = Resistor [tolerance=±5% resistance=220 package=THT]
  R5 = Resistor [tolerance=±5% resistance=220 package=THT]
  R6 = Resistor [tolerance=±5% resistance=220 package=THT]
  R7 = Resistor [tolerance=±5% resistance=220 package=THT]
  R8 = Resistor [tolerance=±5% resistance=220 package=THT]
  R9 = Resistor [tolerance=±5% resistance=220 package=THT]

nets:
  GND: J2.pin1, U6.GND, VCC1.-, C1.-, C2.-, U7.GND, C5.1, C6.1, LED1.anode, LED2.anode, LED3.anode, LED4.anode, R5.Pin_1, R6.Pin_1, R7.Pin_1, R8.Pin_1
  N1: J2.pin2, R9.Pin_1
  N2: U6.input_voltage, VCC1.+, C2.+
  N3: U6.output_voltage, C1.+, U7.VCC, U7.AVCC, U7.AREF, Button1.Pin_3, Button1.Pin_4, Button2.Pin_1, Button2.Pin_2, Button3.Pin_1, Button3.Pin_2, Button4.Pin_1, Button4.Pin_2
  N4: U7.D0_(RX), R9.Pin_0
  N5: U7.D2, Button1.Pin_1, Button1.Pin_2, R5.Pin_0
  N6: U7.D4, Button2.Pin_3, Button2.Pin_4, R6.Pin_0
  N7: U7.XLAT1, XTAL2.pin_0, C5.0
  N8: U7.XLAT2, XTAL2.pin_1, C6.0
  N9: U7.D6_(PWM), Button3.Pin_3, Button3.Pin_4, R7.Pin_0
  N10: U7.D8, Button4.Pin_3, Button4.Pin_4, R8.Pin_0
  N11: U7.D9_(PWM), R4.Pin_1
  N12: U7.D10_(PWM), R3.Pin_1
  N13: U7.D11_(PWM), R2.Pin_1
  N14: U7.D13, R1.Pin_1
  N15: LED1.cathode, R1.Pin_0
  N16: LED2.cathode, R2.Pin_0
  N17: LED3.cathode, R3.Pin_0
  N18: LED4.cathode, R4.Pin_0
